# Fritzing sketch esquema (saved by Fritzing 0.9.4)

parts:
  A1 = Wemos S2 Mini [part_number="WeMos D1 Mini Lite"]
  Component1 = RS485_XY-017 [part_number=XY-017]
  U1 = MLX90614 [package=to-39]
  Componente1 = BME280 Breakout
  J1 = Camdenboss CTB0158-4 [part_number=CTB0158-4 package=THT]

nets:
  VCC: A1.Pin_8, Component1.VCC, U1.VDD, Componente1.3.3V
  N1: A1.Pin_15, U1.PWM_SDA, Componente1.SDI/SDA
  N2: A1.Pin_16, U1.SCL_VZ, Componente1.SCK/SCL
  N3: A1.Pin_17, J1.pin4
  GND: A1.Pin_18, A1.Pin_25, A1.Pin_26, Component1.GND, U1.VSS, Componente1.GND, J1.pin3
  N4: A1.Pin_19, Component1.RXD
  N5: A1.Pin_27, Component1.TXD
  N6: Component1.A, J1.pin1
  N7: Component1.B, J1.pin2

notes:
  Conector circular 4 pin

custom parts:
  Wemos S2 Mini: A mini wifi board based on the ESP32-S2FN4R2.
  RS485_XY-017: Commercially available RS485 to RS232 TTL Module
